// Logisim project CPU.circ as structural Verilog: 10 circuits, main circuit main
module main (
  output [9:0] out_1,
  output [9:0] out_2,
  output [9:0] out_3,
  output [9:0] out_4,
  output [9:0] out_5,
  output [9:0] out_6,
  output [9:0] out_7,
  output ignore,
  output halt
);

  wire alu_1_bnez_2, and_1_out, CLK, clock_1_out, comparator_1_lt, comparator_2_lt, control_unit_1_bnez,
       control_unit_1_halt, control_unit_1_imm, control_unit_1_nop, d_ff_1_qn, not_1_out, t_ff_1_q, TClock;
  wire [1:0] counter_2_q, Upper_2_bits;
  wire [2:0] rom_1_data;
  wire [3:0] b_select_1_sout, control_unit_1_aluop;
  wire [4:0] counter_1_q, multiplexer_1_out, PC_adder_out, PC_Reg_out;
  wire [6:0] adder_1_out, adder_2_out, ASCII, LSB, MiddleBits;
  wire [7:0] multiplexer_4_out;
  wire [9:0] alu_1_out, multiplexer_2_out, multiplexer_3_out;
  wire [31:0] ram_1_data;

  PC_register PC_Reg (.enable(1'b1), .clock(CLK), .val(PC_adder_out), .out(PC_Reg_out));
  PC_adder PC_adder (.PC(PC_Reg_out), .add(multiplexer_1_out), .Out(PC_adder_out));
  RAM #(.addrWidth(24), .dataWidth(32), .bus("separate")) ram_1 (
    .addr({{19{1'b0}}, PC_Reg_out}), .data(ram_1_data), .clk(CLK));  // open: din, str, sel, ld, clr
  D_Flip_Flop d_ff_1 (.clk(CLK), .D(control_unit_1_halt), .Qn(d_ff_1_qn));  // open: Q, preset, en, reset
  Control_Unit control_unit_1 (
    .in_1(ram_1_data[23:19]), .NOP(control_unit_1_nop), .Imm(control_unit_1_imm),
    .aluOp(control_unit_1_aluop), .bnez(control_unit_1_bnez), .HALT(control_unit_1_halt));
  Multiplexer #(.width(5)) multiplexer_1 (
    .in0(5'b00001), .in1(ram_1_data[4:0]), .out(multiplexer_1_out), .sel(alu_1_bnez_2),
    .en(control_unit_1_halt));
  register_bank register_bank_1 (
    .Clock(CLK), .value(alu_1_out), .regSelect(ram_1_data[18:16]), .Enable(control_unit_1_nop), .R0(out_1),
    .R1(out_2), .R2(out_3), .R3(out_4), .R4(out_5), .R5(out_6), .R6(out_7), .clear(d_ff_1_qn));
  B_select b_select_1 (.select(ram_1_data[12:10]), .imm(control_unit_1_imm), .sout(b_select_1_sout));
  Multiplexer #(.select(4), .width(10), .enable("false")) multiplexer_2 (
    .in0(out_1), .in1(out_2), .in2(out_3), .in3(out_4), .in4(out_5), .in5(out_6), .in6(out_7),
    .in7({10{1'b0}}), .in8(ram_1_data[9:0]), .out(multiplexer_2_out), .sel(b_select_1_sout));  // open: in9, in10, in11, in12, in13, in14, in15
  Multiplexer #(.select(3), .width(10), .enable("false")) multiplexer_3 (
    .in0(out_1), .in1(out_2), .in2(out_3), .in3(out_4), .in4(out_5), .in5(out_6), .in6(out_7),
    .out(multiplexer_3_out), .sel(ram_1_data[15:13]));  // open: in7
  ALU alu_1 (
    .select(control_unit_1_aluop), .A(multiplexer_3_out), .B(multiplexer_2_out), .Out(alu_1_out),
    .BNEZ_2(alu_1_bnez_2), .bnez(control_unit_1_bnez));
  TTY #(.rows(33), .cols(4)) tty_1 (.data(ASCII), .clk(TClock));  // open: we, clr
  // Probe on out_1
  // Probe on out_5
  Counter #(.width(5), .max('h1f), .ongoal("stay")) counter_1 (
    .Q(counter_1_q), .carry(halt), .clk(CLK));  // open: load, D, count, clr
  // Probe on out_2
  // Probe on out_6
  Multiplexer #(.select(3), .width(10)) multiplexer_4 (
    .in0(out_1), .in1(out_2), .in2(out_3), .in3(out_4), .in4(out_5), .in5(out_6), .in6(out_7),
    .out({Upper_2_bits, multiplexer_4_out}), .sel(rom_1_data));  // open: in7, en
  not not_1 (not_1_out, halt);
  Clock clock_1 (.out(clock_1_out));
  // Probe on out_3
  // Probe on out_7
  ROM #(.addrWidth(5), .dataWidth(3)) rom_1 (.addr(counter_1_q), .data(rom_1_data));  // open: sel
  and and_1 (and_1_out, not_1_out, clock_1_out);
  not not_2 (TClock, and_1_out);
  // Probe on out_4
  Comparator #(.width(7)) comparator_1 (
    .a(7'b0111001), .b({3'b011, multiplexer_4_out[3:0]}), .lt(comparator_1_lt));  // open: gt, eq
  Comparator #(.width(7)) comparator_2 (
    .a(7'b0111001), .b({3'b011, multiplexer_4_out[7:4]}), .lt(comparator_2_lt));  // open: gt, eq
  T_Flip_Flop t_ff_1 (.clk(and_1_out), .T(1'b1), .Q(t_ff_1_q));  // open: Qn, preset, reset, en
  Counter #(.width(2), .max('h3)) counter_2 (.Q(counter_2_q), .clk(TClock));  // open: load, D, count, carry, clr
  T_Flip_Flop t_ff_2 (.clk(t_ff_1_q), .T(1'b1), .Q(CLK));  // open: Qn, preset, reset, en
  Multiplexer #(.width(7), .disabled(0), .enable("false")) multiplexer_5 (
    .in0({3'b011, multiplexer_4_out[3:0]}), .in1(adder_1_out), .out(LSB), .sel(comparator_1_lt));
  Adder #(.width(7)) adder_1 (
    .a({3'b011, multiplexer_4_out[3:0]}), .b(7'b0000111), .out(adder_1_out));  // open: cin, cout
  Multiplexer #(.width(7), .disabled(0), .enable("false")) multiplexer_6 (
    .in0({3'b011, multiplexer_4_out[7:4]}), .in1(adder_2_out), .out(MiddleBits), .sel(comparator_2_lt));
  Adder #(.width(7)) adder_2 (
    .a({3'b011, multiplexer_4_out[7:4]}), .b(7'b0000111), .out(adder_2_out));  // open: cin, cout
  Multiplexer #(.select(2), .width(7)) multiplexer_7 (
    .in0({5'b01100, Upper_2_bits}), .in1(MiddleBits), .in2(LSB), .in3(7'b0100000), .out(ASCII),
    .sel(counter_2_q));  // open: en
  T_Flip_Flop t_ff_3 (.clk(CLK), .T(1'b1), .Q(ignore));  // open: Qn, preset, reset, en

  // Other names for the same wires on the sheet: R0[9:0] = out_1; R1[9:0] = out_2; R2[9:0] = out_3; R3[9:0] = out_4;
  //   R4[9:0] = out_5; R5[9:0] = out_6; R6[9:0] = out_7

  // Notes on the sheet:
  //   B
  //   A
  //   DO NOT PUT ANY PINS ON THE main circuit.  (You should not need any anyway.)
  //   0F5
  //   0F5
  //   25A
  //   050
  //   2FF
  //   30A
  //   34F
  //   0F5
  //   1EA
  //   07A
  //   29B
  //   165
  //   10F
  //   0F5
  //   0AA
  //   0AA
  //   05A
  //   00A
  //   0FA
  //   104
  //   0B4
  //   165
  //   165
  //   001
  //   001
  //   000
  //   000
  //   000
  //   000
  //   000
  //   ???
  //   There is no Reset.  Just Ctrl-r, then load test.txt into your RAM, and then Ctrl-k
  //   You must  use the CLK tunnel for the source of your clock.  R0-R6 are the other tunnels you need to connect
  //   contents of rom_1 (hex, n*v repeats v):
  //   0 0 0 1 2 3 4 5 6 2 3 4 5 6 0 0 0 1 3 4 6 3 5 5 8*6
endmodule

module _10_bit_register (
  input  enable,
  input  clock,
  input  clear,
  input  [9:0] val,
  output [9:0] out
);

  wire and_1_out;

  and and_1 (and_1_out, enable, clock);
  D_Flip_Flop d_ff_1 (.clk(and_1_out), .D(val[0]), .Q(out[0]), .reset(clear));  // open: Qn, preset, en
  D_Flip_Flop d_ff_2 (.clk(and_1_out), .D(val[1]), .Q(out[1]), .reset(clear));  // open: Qn, preset, en
  D_Flip_Flop d_ff_3 (.clk(and_1_out), .D(val[2]), .Q(out[2]), .reset(clear));  // open: Qn, preset, en
  D_Flip_Flop d_ff_4 (.clk(and_1_out), .D(val[3]), .Q(out[3]), .reset(clear));  // open: Qn, preset, en
  D_Flip_Flop d_ff_5 (.clk(and_1_out), .D(val[4]), .Q(out[4]), .reset(clear));  // open: Qn, preset, en
  D_Flip_Flop d_ff_6 (.clk(and_1_out), .D(val[5]), .Q(out[5]), .reset(clear));  // open: Qn, preset, en
  D_Flip_Flop d_ff_7 (.clk(and_1_out), .D(val[6]), .Q(out[6]), .reset(clear));  // open: Qn, preset, en
  D_Flip_Flop d_ff_8 (.clk(and_1_out), .D(val[7]), .Q(out[7]), .reset(clear));  // open: Qn, preset, en
  D_Flip_Flop d_ff_9 (.clk(and_1_out), .D(val[8]), .Q(out[8]), .reset(clear));  // open: Qn, preset, en
  D_Flip_Flop d_ff_10 (.clk(and_1_out), .D(val[9]), .Q(out[9]), .reset(clear));  // open: Qn, preset, en
endmodule

// Reg Bank
module register_bank (
  input  Clock,
  input  [9:0] value,
  input  [2:0] regSelect,
  input  Enable,
  input  clear,
  output [9:0] R0,
  output [9:0] R1,
  output [9:0] R2,
  output [9:0] R3,
  output [9:0] R4,
  output [9:0] R5,
  output [9:0] R6
);

  wire decoder_1_out0, decoder_1_out1, decoder_1_out2, decoder_1_out3, decoder_1_out4, decoder_1_out5,
       decoder_1_out6;

  Decoder #(.select(3)) decoder_1 (
    .out0(decoder_1_out0), .out1(decoder_1_out1), .out2(decoder_1_out2), .out3(decoder_1_out3),
    .out4(decoder_1_out4), .out5(decoder_1_out5), .out6(decoder_1_out6), .sel(regSelect), .en(Enable));  // open: out7
  // _10_bit_register R0: pin names not known; wires that end beside it: decoder_1_out0, Clock, value, clear, R0
  // _10_bit_register R1: pin names not known; wires that end beside it: decoder_1_out1, Clock, value, clear, clear, R1
  // _10_bit_register R2: pin names not known; wires that end beside it: decoder_1_out2, Clock, value, clear, clear, R2
  // _10_bit_register R3: pin names not known; wires that end beside it: decoder_1_out3, Clock, value, clear, clear, R3
  // _10_bit_register R4: pin names not known; wires that end beside it: decoder_1_out4, Clock, value, clear, clear, R4
  // _10_bit_register R5: pin names not known; wires that end beside it: decoder_1_out5, Clock, value, clear, clear, R5
  _10_bit_register u_R6 (.enable(decoder_1_out6), .clock(Clock), .val(value), .out(R6), .clear(clear));
endmodule

module PC_register (
  input  enable,
  input  clock,
  input  [4:0] val,
  output [4:0] out
);

  wire and_1_out;

  and and_1 (and_1_out, enable, clock);
  D_Flip_Flop d_ff_1 (.clk(and_1_out), .D(val[0]), .Q(out[0]));  // open: Qn, preset, en, reset
  D_Flip_Flop d_ff_2 (.clk(and_1_out), .D(val[1]), .Q(out[1]));  // open: Qn, preset, en, reset
  D_Flip_Flop d_ff_3 (.clk(and_1_out), .D(val[2]), .Q(out[2]));  // open: Qn, preset, en, reset
  D_Flip_Flop d_ff_4 (.clk(and_1_out), .D(val[3]), .Q(out[3]));  // open: Qn, preset, en, reset
  D_Flip_Flop d_ff_5 (.clk(and_1_out), .D(val[4]), .Q(out[4]));  // open: Qn, preset, en, reset
endmodule

module PC_adder (
  input  [4:0] PC,
  input  [4:0] add,
  output [4:0] Out
);

  subtract_lower_bit subtract_lower_bit_1 (.CIN(1'b0), .subtract(add[4]), .out(Out), .A(PC), .B(add));  // open: carry
endmodule

// ctrl unit
module Control_Unit (
  input  [4:0] in_1,
  output NOP,
  output Imm,
  output [3:0] aluOp,
  output bnez,
  output HALT
);

  wire multiplexer_2_out;

  Multiplexer #(.select(5), .width(4), .enable("false")) multiplexer_1 (
    .in0(4'b0000), .in1(4'b0001), .in2(4'b0010), .in3(4'b0011), .in4(4'b0101), .in5(4'b0111), .in6(4'b0110),
    .in7(4'b0100), .in8(4'b0011), .in9(4'b0100), .in10(4'b1000), .out(aluOp), .sel(in_1));  // open: in11, in12, in13, in14, in15, in16, in17, in18, in19, in20, in21, in22, in23, in24, in25, in26, in27, in28, in29, in30, in31
  Multiplexer #(.select(5), .enable("false")) multiplexer_2 (
    .in0(1'b0), .in1(1'b0), .in2(1'b0), .in3(1'b0), .in4(1'b0), .in5(1'b0), .in6(1'b0), .in7(1'b0),
    .in8(1'b0), .in9(1'b0), .in10(1'b0), .in11(1'b0), .in12(1'b1), .in13(1'b0), .in14(1'b0), .in15(1'b0),
    .in16(1'b0), .in17(1'b0), .in18(1'b0), .in19(1'b0), .in20(1'b0), .in21(1'b0), .in22(1'b0), .in23(1'b0),
    .in24(1'b0), .in25(1'b0), .in26(1'b0), .in27(1'b0), .in28(1'b0), .in29(1'b0), .in30(1'b0), .in31(1'b0),
    .out(multiplexer_2_out), .sel(in_1));
  not not_1 (NOP, multiplexer_2_out);
  Multiplexer #(.select(5), .enable("false")) multiplexer_3 (
    .in0(1'b1), .in1(1'b1), .in2(1'b1), .in3(1'b1), .in4(1'b1), .in5(1'b1), .in6(1'b1), .in7(1'b1),
    .in8(1'b1), .in9(1'b1), .in10(1'b1), .in11(1'b1), .in12(1'b1), .in13(1'b1), .in14(1'b1), .in15(1'b1),
    .in16(1'b1), .in17(1'b1), .in18(1'b1), .in19(1'b1), .in20(1'b1), .in21(1'b1), .in22(1'b1), .in23(1'b1),
    .in24(1'b1), .in25(1'b1), .in26(1'b1), .in27(1'b1), .in28(1'b1), .in29(1'b1), .in30(1'b1), .in31(1'b0),
    .out(HALT), .sel(in_1));
  Multiplexer #(.select(5), .enable("false")) multiplexer_4 (
    .in0(1'b0), .in1(1'b0), .in2(1'b0), .in3(1'b0), .in4(1'b0), .in5(1'b0), .in6(1'b0), .in7(1'b0),
    .in8(1'b0), .in9(1'b0), .in10(1'b0), .in11(1'b1), .in12(1'b0), .in13(1'b0), .in14(1'b0), .in15(1'b0),
    .in16(1'b0), .in17(1'b0), .in18(1'b0), .in19(1'b0), .in20(1'b0), .in21(1'b0), .in22(1'b0), .in23(1'b0),
    .in24(1'b0), .in25(1'b0), .in26(1'b0), .in27(1'b0), .in28(1'b0), .in29(1'b0), .in30(1'b0), .in31(1'b0),
    .out(bnez), .sel(in_1));
  Multiplexer #(.select(5), .enable("false")) multiplexer_5 (
    .in0(1'b0), .in1(1'b0), .in2(1'b0), .in3(1'b0), .in4(1'b0), .in5(1'b0), .in6(1'b0), .in7(1'b0),
    .in8(1'b1), .in9(1'b1), .in10(1'b1), .in11(1'b0), .in12(1'b0), .in13(1'b0), .in14(1'b0), .in15(1'b0),
    .in16(1'b0), .in17(1'b0), .in18(1'b0), .in19(1'b0), .in20(1'b0), .in21(1'b0), .in22(1'b0), .in23(1'b0),
    .in24(1'b0), .in25(1'b0), .in26(1'b0), .in27(1'b0), .in28(1'b0), .in29(1'b0), .in30(1'b0), .in31(1'b0),
    .out(Imm), .sel(in_1));
endmodule

module ALU (
  input  [3:0] select,
  input  bnez,
  input  [9:0] A,
  input  [9:0] B,
  output [9:0] Out,
  output BNEZ_2
);

  wire or_2_out;
  wire [9:0] and_1_result, Copy_out_4, n10_bit_add_1_out_4, n10_bit_adder_1_out_4, n10_bit_adder_2_out_4,
       not_1_result, or_1_result;

  AND and_1 (.A(A), .B(B), .Result(and_1_result));
  OR or_1 (.A(A), .B(B), .Result(or_1_result));
  NOT not_1 (.A(A), .Result(not_1_result));
  _10_bit_adder u_10_bit_adder_1 (.CIN(1'b0), .out_4(n10_bit_adder_1_out_4), .A(A), .B(B));
  _10_bit_adder u_10_bit_adder_2 (.CIN(1'b1), .out_4(n10_bit_adder_2_out_4), .A(A), .B(B));
  _10_bit_add u_10_bit_add_1 (.CIN(1'b0), .out_4(n10_bit_add_1_out_4), .A(A), .B({10{1'b0}}));
  _10_bit_add Copy (.CIN(1'b0), .out_4(Copy_out_4), .A(B), .B({10{1'b0}}));
  Multiplexer #(.select(4), .width(10), .enable("false")) multiplexer_1 (
    .in0(and_1_result), .in1(or_1_result), .in2(not_1_result), .in3(n10_bit_adder_1_out_4),
    .in4(n10_bit_adder_2_out_4), .in5(n10_bit_add_1_out_4), .in6({1'b0, A[9:1]}), .in7({A[8:0], 1'b0}),
    .in8(Copy_out_4), .out(Out), .sel(select));  // open: in9, in10, in11, in12, in13, in14, in15
  or or_2 (or_2_out, B[0], B[1], B[2], B[3], B[4], B[5], B[6], B[7], B[8], B[9]);
  and and_2 (BNEZ_2, bnez, or_2_out);
endmodule

module B_select (
  input  [2:0] select,
  input  imm,
  output [3:0] sout
);

  Multiplexer #(.width(4), .enable("false")) multiplexer_1 (
    .in0({1'b0, select}), .in1({imm, 3'b000}), .out(sout), .sel(imm));
endmodule

module _10_bit_adder (
  input  CIN,
  input  [9:0] A,
  input  [9:0] B,
  output [9:0] out_4
);

  wire n5_bit_add_1_carry;

  _5_bit_add u_5_bit_add_1 (.CIN(CIN), .out(out_4[4:0]), .carry(n5_bit_add_1_carry), .A(A[4:0]), .B(B[4:0]));
  subtract_lower_bit subtract_lower_bit_1 (
    .CIN(n5_bit_add_1_carry), .subtract(CIN), .out(out_4[9:5]), .A(A[9:5]), .B(B[9:5]));  // open: carry
endmodule

module subtract_lower_bit (
  input  CIN,
  input  subtract,
  input  [4:0] A,
  input  [4:0] B,
  output [4:0] out,
  output carry
);

  wire add_1_gi, add_1_pi, add_2_gi, add_2_pi, add_3_gi, add_3_pi, add_4_gi, add_4_pi, add_5_gi, add_5_pi,
       addcarry_1_c1, addcarry_1_c2, addcarry_1_c3, addcarry_1_c4, xor_1_out, xor_2_out, xor_3_out,
       xor_4_out, xor_5_out;

  xor xor_1 (xor_1_out, subtract, B[0]);
  xor xor_2 (xor_2_out, subtract, B[1]);
  xor xor_3 (xor_3_out, subtract, B[2]);
  xor xor_4 (xor_4_out, subtract, B[3]);
  xor xor_5 (xor_5_out, subtract, B[4]);
  ADD add_1 (.pi(add_1_pi), .gi(add_1_gi), .Cin(CIN), .A(A[0]), .B(xor_1_out), .result(out[0]));
  ADD add_2 (.pi(add_2_pi), .gi(add_2_gi), .Cin(addcarry_1_c1), .A(A[1]), .B(xor_2_out), .result(out[1]));
  ADD add_3 (.pi(add_3_pi), .gi(add_3_gi), .Cin(addcarry_1_c2), .A(A[2]), .B(xor_3_out), .result(out[2]));
  ADD add_4 (.pi(add_4_pi), .gi(add_4_gi), .Cin(addcarry_1_c3), .A(A[3]), .B(xor_4_out), .result(out[3]));
  ADD add_5 (.pi(add_5_pi), .gi(add_5_gi), .Cin(addcarry_1_c4), .A(A[4]), .B(xor_5_out), .result(out[4]));
  addCarry addcarry_1 (
    .C0(CIN), .P0(add_1_pi), .G0(add_1_gi), .P1(add_2_pi), .G1(add_2_gi), .P2(add_3_pi), .G2(add_3_gi),
    .P3(add_4_pi), .G3(add_4_gi), .P4(add_5_pi), .G4(add_5_gi), .C1(addcarry_1_c1), .C2(addcarry_1_c2),
    .C3(addcarry_1_c3), .C4(addcarry_1_c4), .C5(carry));
endmodule
