// Logisim project aluSUB.circ as structural Verilog: 9 circuits, main circuit main
module main (
);

  wire A0, A1, A2, A3, A4, B0, B1, B2, B3, B4, C0, C1, C2, C3, C4, C5, CIN, clock_1_out, clock_2_out, go,
       HCLK, not_1_out, reset, S0, S1;
  wire [2:0] multiplexer_1_out;
  wire [6:1] counter_1_q;

  // alu alu_1: pin names not known; wires that end beside it: CIN, A0, B0, A1, B1, A2, B2, {S1, S0}, C0, C1, C2, C3, C4
  // Probe on {C5, C4, C3}
  // Probe on {4'b0110, multiplexer_1_out}
  // Probe on {C2, C1, C0}
  Multiplexer #(.width(3)) multiplexer_1 (
    .in0({C5, C4, C3}), .in1({C2, C1, C0}), .out(multiplexer_1_out), .sel(HCLK));  // open: en
  // Probe on multiplexer_1_out
  Clock clock_1 (.out(clock_1_out));
  TTY #(.rows(32), .cols(2)) tty_1 (.data({4'b0110, multiplexer_1_out}), .clk(clock_1_out), .we(go), .clr(reset));
  // Probe on {A4, A3, A2, A1, A0, CIN}
  // Probe on {B4, B3, B2, B1, B0}
  Clock clock_2 (.out(clock_2_out));
  // Probe on S1
  Counter #(.width(7), .max('h7f), .ongoal("stay")) counter_1 (
    .Q({counter_1_q, HCLK}), .clk(clock_2_out), .clr(reset));  // open: load, D, count, carry
  // Probe on S0
  Button u_Reset (.out(reset));
  not not_1 (not_1_out, HCLK);
  not not_2 (go, counter_1_q[6]);
  Random #(.width(13), .seed(34573)) random_1 (
    .clk(not_1_out), .next(go), .out({B4, B3, B2, B1, B0, A4, A3, A2, A1, A0, CIN, S1, S0}), .clr(reset));

  // Notes on the sheet:
  //   07
  //   51
  //   40
  //   51
  //   77
  //   77
  //   57
  //   63
  //   43
  //   77
  //   60
  //   51
  //   46
  //   71
  //   32
  //   43
  //   34
  //   50
  //   53
  //   00
  //   07
  //   02
  //   74
  //   04
  //   35
  //   52
  //   52
  //   50
  //   65
  //   46
  //   11
  //   57
endmodule

module AND (
  input  [9:0] A,
  input  [9:0] B,
  output [9:0] Result
);

  and _1 (Result[0], A[0], B[0]);
  and _2 (Result[1], A[1], B[1]);
  and _3 (Result[2], A[2], B[2]);
  and _4 (Result[3], A[3], B[3]);
  and _5 (Result[4], A[4], B[4]);
  and _1_2 (Result[5], A[5], B[5]);
  and _2_2 (Result[6], A[6], B[6]);
  and _3_2 (Result[7], A[7], B[7]);
  and _4_2 (Result[8], A[8], B[8]);
  and _5_2 (Result[9], A[9], B[9]);
endmodule

module OR (
  input  [9:0] A,
  input  [9:0] B,
  output [9:0] Result
);

  or or_1 (Result[0], A[0], B[0]);
  or or_2 (Result[1], A[1], B[1]);
  or or_3 (Result[2], A[2], B[2]);
  or or_4 (Result[3], A[3], B[3]);
  or or_5 (Result[4], A[4], B[4]);
  or or_6 (Result[5], A[5], B[5]);
  or or_7 (Result[6], A[6], B[6]);
  or or_8 (Result[7], A[7], B[7]);
  or or_9 (Result[8], A[8], B[8]);
  or or_10 (Result[9], A[9], B[9]);
endmodule

module NOT (
  input  [9:0] A,
  output [9:0] Result
);

  not not_1 (Result[0], A[0]);
  not not_2 (Result[1], A[1]);
  not not_3 (Result[2], A[2]);
  not not_4 (Result[3], A[3]);
  not not_5 (Result[4], A[4]);
  not not_6 (Result[5], A[5]);
  not not_7 (Result[6], A[6]);
  not not_8 (Result[7], A[7]);
  not not_9 (Result[8], A[8]);
  not not_10 (Result[9], A[9]);
endmodule

module ADD (
  input  Cin,
  input  A,
  input  B,
  output result,
  output pi,
  output gi
);

  wire xor_1_out;

  xor xor_1 (xor_1_out, A, B);
  and and_1 (gi, A, B);
  xor xor_2 (result, xor_1_out, Cin);
  or or_1 (pi, A, B);
endmodule

module alu (
  input  [2:0] select,
  input  [9:0] A,
  input  [9:0] B,
  output [9:0] out_4
);

  wire [9:0] and_1_result, n10_bit_add_1_out_4, n10_bit_add_2_out_4, not_1_result, or_1_result;

  AND and_1 (.A(A), .B(B), .Result(and_1_result));
  OR or_1 (.A(A), .B(B), .Result(or_1_result));
  NOT not_1 (.A(A), .Result(not_1_result));
  _10_bit_add u_10_bit_add_1 (.CIN(1'b0), .out_4(n10_bit_add_1_out_4), .A(A), .B(B));
  _10_bit_add u_10_bit_add_2 (.CIN(1'b1), .out_4(n10_bit_add_2_out_4), .A(A), .B(B));
  Multiplexer #(.select(3), .width(10)) multiplexer_1 (
    .in0(and_1_result), .in1(or_1_result), .in2(not_1_result), .in3(n10_bit_add_1_out_4),
    .in4(n10_bit_add_2_out_4), .out(out_4), .sel(select));  // open: in5, in6, in7, en
endmodule

module addCarry (
  input  C0,
  input  P0,
  input  G0,
  input  P1,
  input  G1,
  input  P2,
  input  G2,
  input  P3,
  input  G3,
  input  P4,
  input  G4,
  output C1,
  output C2,
  output C3,
  output C4,
  output C5
);

  wire and_1_out, and_2_out, and_3_out, and_4_out, and_5_out, and_6_out, and_7_out, and_8_out, and_9_out,
       and_10_out, and_11_out, and_12_out, and_13_out, and_14_out, and_15_out;

  and and_1 (and_1_out, P0, C0);
  and and_2 (and_2_out, G1, P2, P3);
  and and_3 (and_3_out, G2, P3);
  and and_4 (and_4_out, G0, P1, P2, P3);
  and and_5 (and_5_out, C0, P0, P2, P3);
  or or_1 (C1, and_1_out, G0);
  and and_6 (and_6_out, P0, P0, P1, C0);
  and and_7 (and_7_out, P1, G0);
  and and_8 (and_8_out, P4, P3, P1, P0, C0);
  and and_9 (and_9_out, G0, P1, P2, P3, P4);
  and and_10 (and_10_out, G1, P2, P3, P4);
  and and_11 (and_11_out, G2, P3, P4);
  and and_12 (and_12_out, G3, P4);
  and and_13 (and_13_out, G1, P2);
  and and_14 (and_14_out, P2, P1, G0);
  and and_15 (and_15_out, P2, P1, P0, C0);
  or or_2 (C2, and_6_out, and_7_out, G1);
  or or_3 (C4, and_2_out, and_3_out, and_5_out, and_4_out, G3);
  or or_4 (C3, and_13_out, G2, and_14_out, and_15_out);
  or or_5 (C5, and_8_out, and_9_out, and_10_out, and_11_out, and_12_out, G4);
endmodule

module _5_bit_add (
  input  CIN,
  input  [4:0] A,
  input  [4:0] B,
  output [4:0] out,
  output carry
);

  wire add_1_gi, add_1_pi, add_2_gi, add_2_pi, add_3_gi, add_3_pi, add_4_gi, add_4_pi, add_5_gi, add_5_pi,
       addcarry_1_c1, addcarry_1_c2, addcarry_1_c3, addcarry_1_c4, xor_1_out, xor_2_out, xor_3_out,
       xor_4_out, xor_5_out;

  xor xor_1 (xor_1_out, CIN, B[0]);
  xor xor_2 (xor_2_out, CIN, B[1]);
  xor xor_3 (xor_3_out, CIN, B[2]);
  xor xor_4 (xor_4_out, CIN, B[3]);
  xor xor_5 (xor_5_out, CIN, B[4]);
  ADD add_1 (.pi(add_1_pi), .gi(add_1_gi), .Cin(CIN), .A(A[0]), .B(xor_1_out), .result(out[0]));
  ADD add_2 (.pi(add_2_pi), .gi(add_2_gi), .Cin(addcarry_1_c1), .A(A[1]), .B(xor_2_out), .result(out[1]));
  ADD add_3 (.pi(add_3_pi), .gi(add_3_gi), .Cin(addcarry_1_c2), .A(A[2]), .B(xor_3_out), .result(out[2]));
  ADD add_4 (.pi(add_4_pi), .gi(add_4_gi), .Cin(addcarry_1_c3), .A(A[3]), .B(xor_4_out), .result(out[3]));
  ADD add_5 (.pi(add_5_pi), .gi(add_5_gi), .Cin(addcarry_1_c4), .A(A[4]), .B(xor_5_out), .result(out[4]));
  addCarry addcarry_1 (
    .C0(CIN), .P0(add_1_pi), .G0(add_1_gi), .P1(add_2_pi), .G1(add_2_gi), .P2(add_3_pi), .G2(add_3_gi),
    .P3(add_4_pi), .G3(add_4_gi), .P4(add_5_pi), .G4(add_5_gi), .C1(addcarry_1_c1), .C2(addcarry_1_c2),
    .C3(addcarry_1_c3), .C4(addcarry_1_c4), .C5(carry));
endmodule

module _10_bit_add (
  input  CIN,
  input  [9:0] A,
  input  [9:0] B,
  output [9:0] out_4
);

  wire n5_bit_add_1_carry;

  _5_bit_add u_5_bit_add_1 (.CIN(CIN), .out(out_4[4:0]), .carry(n5_bit_add_1_carry), .A(A[4:0]), .B(B[4:0]));
  _5_bit_add u_5_bit_add_2 (.CIN(n5_bit_add_1_carry), .out(out_4[9:5]), .A(A[9:5]), .B(B[9:5]));  // open: carry
endmodule
